// Logisim project adder_subtractor(mil-1).circ as structural Verilog: 3 circuits, main circuit full adder
module full_adder (
  input  M,
  input  A,
  input  B,
  output Sum,
  output Carry
);

  wire and_1_out, and_2_out, xor_1_out;

  xor xor_1 (xor_1_out, M, A);
  and and_1 (and_1_out, M, A);
  and and_2 (and_2_out, xor_1_out, B);
  xor xor_2 (Sum, xor_1_out, B);
  or or_1 (Carry, and_1_out, and_2_out);
endmodule

module _4_bit_adder_subtractor (
  input  M,
  input  B3,
  input  B2,
  input  B1,
  input  B0,
  input  in_6,
  input  in_7,
  input  A3,
  input  A2,
  input  A1,
  input  A0,
  output C3,
  output S3,
  output S2,
  output S1,
  output S0
);

  wire full_adder_2_carry, full_adder_3_carry, full_adder_4_carry, multiplexer_1_out,
       seven_segment_decoder_and_display_1_a_2, seven_segment_decoder_and_display_1_b_2,
       seven_segment_decoder_and_display_1_c_2, seven_segment_decoder_and_display_1_d_2,
       seven_segment_decoder_and_display_1_e, seven_segment_decoder_and_display_1_f,
       seven_segment_decoder_and_display_1_g, xor_1_out, xor_2_out, xor_3_out, xor_4_out;

  LED led_1 (.in(C3));
  full_adder full_adder_1 (.M(full_adder_2_carry), .A(A3), .B(xor_1_out), .Sum(S3), .Carry(C3));
  xor xor_1 (xor_1_out, B3, multiplexer_1_out);
  LED led_2 (.in(S3));
  xor xor_2 (xor_2_out, B2, multiplexer_1_out);
  full_adder full_adder_2 (.M(full_adder_3_carry), .A(A2), .B(xor_2_out), .Sum(S2), .Carry(full_adder_2_carry));
  LED led_3 (.in(S2));
  xor xor_3 (xor_3_out, B1, multiplexer_1_out);
  full_adder full_adder_3 (.M(full_adder_4_carry), .A(A1), .B(xor_3_out), .Sum(S1), .Carry(full_adder_3_carry));
  LED led_4 (.in(S1));
  Seven_Segment_Decoder_and_Display seven_segment_decoder_and_display_1 (
    .A(S0), .B(S1), .C(S2), .D(S3), .a_2(seven_segment_decoder_and_display_1_a_2),
    .b_2(seven_segment_decoder_and_display_1_b_2), .c_2(seven_segment_decoder_and_display_1_c_2),
    .d_2(seven_segment_decoder_and_display_1_d_2), .e(seven_segment_decoder_and_display_1_e),
    .f(seven_segment_decoder_and_display_1_f), .g(seven_segment_decoder_and_display_1_g));
  xor xor_4 (xor_4_out, B0, multiplexer_1_out);
  full_adder full_adder_4 (.M(multiplexer_1_out), .A(A0), .B(xor_4_out), .Sum(S0), .Carry(full_adder_4_carry));
  LED led_5 (.in(S0));
  _7_Segment_Display u_7_segment_display_1 (
    .g(seven_segment_decoder_and_display_1_g), .f(seven_segment_decoder_and_display_1_f),
    .a(seven_segment_decoder_and_display_1_a_2), .b(seven_segment_decoder_and_display_1_b_2),
    .e(seven_segment_decoder_and_display_1_e), .d(seven_segment_decoder_and_display_1_d_2),
    .c(seven_segment_decoder_and_display_1_c_2));  // open: dp
  LED led_6 (.in(multiplexer_1_out));
  Multiplexer multiplexer_1 (.in0(in_6), .in1(in_7), .out(multiplexer_1_out), .sel(M));  // open: en

  // Notes on the sheet:
  //   Full adder
  //   C2
  //   Full adder
  //   C1
  //   Full adder
  //   C0
  //   Full adder
endmodule

module Seven_Segment_Decoder_and_Display (
  input  A,
  input  B,
  input  C,
  input  D,
  output a_2,
  output b_2,
  output c_2,
  output d_2,
  output e,
  output f,
  output g
);

  wire and_1_out, and_2_out, and_3_out, and_4_out, and_5_out, and_6_out, and_7_out, and_8_out, and_9_out,
       and_10_out, and_11_out, and_12_out, and_13_out, and_14_out, and_15_out, and_16_out, not_1_out,
       not_2_out, not_3_out, not_4_out, not_5_out, not_6_out, not_7_out, not_8_out, not_9_out, not_10_out,
       not_11_out, not_12_out, not_13_out, not_14_out, not_15_out, not_16_out, not_17_out, not_18_out,
       not_19_out, not_20_out, not_21_out;

  not not_1 (not_1_out, A);
  and and_1 (and_1_out, not_1_out, not_2_out);
  not not_2 (not_2_out, C);
  and and_2 (and_2_out, A, C);
  not not_3 (not_3_out, A);
  and and_3 (and_3_out, not_3_out, not_4_out);
  not not_4 (not_4_out, B);
  not not_5 (not_5_out, C);
  and and_4 (and_4_out, A, B);
  not not_6 (not_6_out, B);
  or or_1 (c_2, not_6_out, C, A);
  not not_7 (not_7_out, A);
  and and_5 (and_5_out, not_7_out, not_8_out);
  not not_8 (not_8_out, C);
  not not_9 (not_9_out, A);
  and and_6 (and_6_out, not_9_out, B);
  and and_7 (and_7_out, B, not_10_out);
  not not_10 (not_10_out, C);
  and and_8 (and_8_out, A, not_11_out, C);
  not not_11 (not_11_out, B);
  not not_12 (not_12_out, A);
  and and_9 (and_9_out, not_12_out, not_13_out);
  not not_13 (not_13_out, C);
  not not_14 (not_14_out, A);
  and and_10 (and_10_out, not_14_out, B);
  not not_15 (not_15_out, A);
  and and_11 (and_11_out, not_15_out, not_16_out);
  not not_16 (not_16_out, B);
  not not_17 (not_17_out, A);
  and and_12 (and_12_out, not_17_out, C);
  not not_18 (not_18_out, B);
  and and_13 (and_13_out, not_18_out, C);
  not not_19 (not_19_out, B);
  and and_14 (and_14_out, not_19_out, C);
  not not_20 (not_20_out, A);
  and and_15 (and_15_out, not_20_out, B);
  and and_16 (and_16_out, B, not_21_out);
  not not_21 (not_21_out, C);
  or or_2 (a_2, and_1_out, D, B, and_2_out);
  or or_3 (b_2, and_3_out, not_5_out, and_4_out);
  or or_4 (d_2, and_5_out, D, and_6_out, and_7_out, and_8_out);
  or or_5 (e, and_9_out, and_10_out);
  or or_6 (f, and_11_out, D, and_12_out, and_13_out);
  or or_7 (g, D, and_14_out, and_15_out, and_16_out);
endmodule
